# Fritzing sketch prlsys (saved by Fritzing 0.9.3b)
breadboards: 1

parts:
  Part1 = Arduino Uno (Rev3) - ICSP
  J2 = Basic Servo
  J3 = Basic Servo
  Part2 = InvenSense MPU6050
  Mod1 = Raspberry Pi Pico
  A2 = NEO-6M GPS Module [part_number=GY-GPS6MV2]
  U1 = LM2596 step down module
  U2 = LIPO-1000mAh [package=lipo-1000]

nets:
  N1: Part1.A4/SDA, Part2.SDA
  N2: Part1.A5/SCL, Part2.SCL
  GND: Part1.GND, J2.gnd, J3.gnd, Part2.GND, Mod1.pin_3, Mod1.pin_23, Mod1.pin_33, Mod1.pin_42, A2.GND, U1.IN-, U1.OUT-, U2.-
  N3: Part1.D9_PWM, J2.pulse
  N4: Part1.D10_PWM/SS, J3.pulse
  N5: Part1.D2, Mod1.pin_17
  N6: Part1.D3_PWM, Mod1.pin_16
  VCC: Part1.5V, J2.vcc, J3.vcc, Part2.VCC, A2.Vcc, U1.OUT+
  N7: Mod1.pin_6, A2.Rx
  N8: Mod1.pin_7, A2.Tx
  N9: U1.IN+, U2.+

custom parts:
  Raspberry Pi Pico: Raspberry Pi Pico. Based around the RP2040 microcontroller the Pico is a low cost microcontroller device bringing Raspberry Pi quality, cost, and easy of use to the microcontroller space. Jan 2021, Split part in to two versions: tht (this one) and SMD. This one will drill holes for a .1 in header in pcb to allow plugging in the module as well as providing pads to solder the module to the top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
  NEO-6M GPS Module: GY-GPS6MV2 NEO-6M GPS Module Module based on U-blox NEO-6M GPS engine, incorporating regulator for 3.3-5V DC input, MS621FE-compatible rechargeable battery for backup and EEPROM for storing configuration settings. Links: NEO-6 series product information page NEO-6 Datasheet
  LM2596 step down module: LM2596 DC-DC step down power supply module 3 A.
